# Fritzing sketch Esquema de conexion (saved by Fritzing 0.9.8b)
breadboards: 1

parts:
  LCD1 = LCD screen  # not connected
  ZS-042_RTC1 = ZS-042 RTC Module
  J1 = Piezo Speaker
  LED1 = smd LED [color="Red (633nm)" package="1206 [SMD]"]
  R1 = Resistor [tolerance=±5% resistance=220 package="0402 [SMD]"]  # not connected
  J2 = Basic Servo
  J3 = Basic Servo
  J4 = Basic Servo
  J5 = Basic Servo
  Componente3 = Arduino Uno (Rev3)
  LED2 = smd LED [color="Green (565nm)" package="1206 [SMD]"]

nets:
  GND: ZS-042_RTC1.GND, J1.pin1, LED1.cathode, J2.gnd, J3.gnd, J4.gnd, Componente3.GND, LED2.cathode
  VCC: ZS-042_RTC1.VCC, J2.vcc, J3.vcc, J4.vcc, Componente3.5V
  N1: ZS-042_RTC1.SDA, Componente3.A4/SDA
  N2: ZS-042_RTC1.SCL, Componente3.A5/SCL
  N3: J1.pin2, Componente3.D11_PWM/MOSI
  N4: LED1.anode, Componente3.D13/SCK
  N5: J2.pulse, Componente3.D3_PWM
  N6: J3.pulse, Componente3.D2
  N7: J4.pulse, Componente3.D1/TX
  N8: J5.pulse, Componente3.D0/RX
  N9: Componente3.D12/MISO, LED2.anode

// code stored in the sketch: 1.ino
void setup(){
pinMode()
}
